// Logisim project Practica03.circ as structural Verilog: 12 circuits, main circuit main
module main (
);

  wire CLK, control_1_alusrc, control_1_memread, control_1_memtoreg, control_1_memwrite, control_1_regdst,
       control_1_regwrite, Reset;
  wire [1:0] control_1_aluop;
  wire [2:0] alucontrol_1_op;
  wire [4:0] ildown_1_rd, ildown_1_rs, ildown_1_rt, multiplexer_1_out;
  wire [5:0] ildown_1_op;
  wire [15:0] ildown_1_imm;
  wire [31:0] alu_1_result, data_memory_1_read_data, fetch_1_instruction, multiplexer_2_out,
       multiplexer_3_out, reg_file_1_read_data1, reg_file_1_read_data2, sign_ext_1_out32bit, undriven;

  Button u_Reset (.out(Reset));
  Clock clock_1 (.out(CLK));
  Fetch fetch_1 (.PCnext(undriven), .CLK(CLK), .Reset(Reset), .Instruction(fetch_1_instruction));  // open: PC, PCplus4
  Ildown ildown_1 (
    .Instruction(fetch_1_instruction), .imm(ildown_1_imm), .rd(ildown_1_rd), .rt(ildown_1_rt),
    .rs(ildown_1_rs), .op(ildown_1_op));  // open: address, funct, shamt
  control control_1 (
    .OP(ildown_1_op), .RegDst(control_1_regdst), .ALUSrc(control_1_alusrc), .MemtoReg(control_1_memtoreg),
    .RegWrite(control_1_regwrite), .MemRead(control_1_memread), .MemWrite(control_1_memwrite),
    .ALUop(control_1_aluop));  // open: Branch, Jump, Link
  Multiplexer #(.width(5)) multiplexer_1 (
    .in0(ildown_1_rt), .in1(ildown_1_rd), .out(multiplexer_1_out), .sel(control_1_regdst));
  Shift_left2 shift_left2_1 (.In32bit(sign_ext_1_out32bit));  // open: Out32bit
  Reg_File reg_file_1 (
    .Read_Reg1(ildown_1_rs), .Read_Reg2(ildown_1_rt), .Reg_Write(control_1_regwrite),
    .Write_Reg(multiplexer_1_out), .Write_Data(multiplexer_3_out), .CLK(CLK), .Reset(Reset),
    .Read_Data1(reg_file_1_read_data1), .Read_Data2(reg_file_1_read_data2));
  Sign_Ext sign_ext_1 (.In16bit(ildown_1_imm), .Out32bit(sign_ext_1_out32bit));
  ALUControl alucontrol_1 (.ALUop(control_1_aluop), .Funct(ildown_1_imm[5:0]), .Op(alucontrol_1_op));
  Multiplexer #(.width(32)) multiplexer_2 (
    .in0(reg_file_1_read_data2), .in1(sign_ext_1_out32bit), .out(multiplexer_2_out), .sel(control_1_alusrc));
  Adder #(.width(32)) adder_1 ();  // open: a, b, out, cin, cout
  ALU alu_1 (
    .In1(reg_file_1_read_data1), .In2(multiplexer_2_out), .ALU_Operation(alucontrol_1_op),
    .Result(alu_1_result));  // open: Zero
  Data_memory data_memory_1 (
    .Address(alu_1_result), .MemWrite(control_1_memwrite), .MemRead(control_1_memread), .CLK(CLK),
    .Read_data(data_memory_1_read_data));  // open: MemInput
  // AND_Gate and_1 is placed but not wired
  Multiplexer #(.width(32)) multiplexer_3 (
    .in0(data_memory_1_read_data), .out(multiplexer_3_out), .sel(control_1_memtoreg));  // open: in1
endmodule

module Fetch (
  input  [31:0] PCnext,
  input  CLK,
  input  Reset,
  output [31:0] PC,
  output [31:0] PCplus4,
  output [31:0] Instruction
);

  wire [23:0] division_4_1_o;

  Register #(.width(32)) PCreg (.D(PCnext), .en(1'b1), .clk(CLK), .Q(PC), .clr(Reset));
  // Probe on PC
  Adder #(.width(32)) adder_1 (.a(PC), .b(32'h4), .out(PCplus4));  // open: cin, cout
  division_4 division_4_1 (.i(PC), .o(division_4_1_o));
  ROM #(.addrWidth(24), .dataWidth(32)) rom_1 (.addr(division_4_1_o), .data(Instruction));
  // Probe on PCplus4
  // Probe on division_4_1_o
  // Probe on Instruction

  // Notes on the sheet:
  //   contents of rom_1 (hex, n*v repeats v):
  //   112345 0 cab4
endmodule

module Ildown (
  input  [31:0] Instruction,
  output [25:0] address,
  output [15:0] imm,
  output [5:0] funct,
  output [4:0] shamt,
  output [4:0] rd,
  output [4:0] rt,
  output [4:0] rs,
  output [5:0] op
);


  assign address = Instruction[25:0];
  assign funct = Instruction[5:0];
  assign imm = Instruction[15:0];
  assign op = Instruction[31:26];
  assign rd = Instruction[15:11];
  assign rs = Instruction[25:21];
  assign rt = Instruction[20:16];
  assign shamt = Instruction[10:6];
endmodule

module Reg_File (
  input  [4:0] Read_Reg1,
  input  [4:0] Read_Reg2,
  input  Reg_Write,
  input  [4:0] Write_Reg,
  input  [31:0] Write_Data,
  input  CLK,
  input  Reset,
  output [31:0] Read_Data1,
  output [31:0] Read_Data2
);

  wire decoder_1_out0, decoder_1_out1, decoder_1_out2, decoder_1_out3, decoder_1_out4, decoder_1_out5,
       decoder_1_out6, decoder_1_out7, decoder_1_out8, decoder_1_out9, decoder_1_out10, decoder_1_out11,
       decoder_1_out12, decoder_1_out13, decoder_1_out14, decoder_1_out15, decoder_1_out16, decoder_1_out17,
       decoder_1_out18, decoder_1_out19, decoder_1_out20, decoder_1_out21, decoder_1_out22, decoder_1_out23,
       decoder_1_out24, decoder_1_out25, decoder_1_out26, decoder_1_out27, decoder_1_out28, decoder_1_out29,
       decoder_1_out30, decoder_1_out31;
  wire [31:0] a0, a1, a2, a3, at, fp, gp, k0, k1, ra, s0, s1, s2, s3, s4, s5, s6, s7, sp, t0, t1, t2, t3, t4,
       t5, t6, t7, t8, t9, v0, v1, zero;

  Decoder #(.select(5)) decoder_1 (
    .out0(decoder_1_out0), .out1(decoder_1_out1), .out2(decoder_1_out2), .out3(decoder_1_out3),
    .out4(decoder_1_out4), .out5(decoder_1_out5), .out6(decoder_1_out6), .out7(decoder_1_out7),
    .out8(decoder_1_out8), .out9(decoder_1_out9), .out10(decoder_1_out10), .out11(decoder_1_out11),
    .out12(decoder_1_out12), .out13(decoder_1_out13), .out14(decoder_1_out14), .out15(decoder_1_out15),
    .out16(decoder_1_out16), .out17(decoder_1_out17), .out18(decoder_1_out18), .out19(decoder_1_out19),
    .out20(decoder_1_out20), .out21(decoder_1_out21), .out22(decoder_1_out22), .out23(decoder_1_out23),
    .out24(decoder_1_out24), .out25(decoder_1_out25), .out26(decoder_1_out26), .out27(decoder_1_out27),
    .out28(decoder_1_out28), .out29(decoder_1_out29), .out30(decoder_1_out30), .out31(decoder_1_out31),
    .sel(Write_Reg), .en(Reg_Write));
  Register #(.width(32)) u_zero (.D({32{1'b0}}), .en(decoder_1_out0), .clk(CLK), .Q(zero), .clr(Reset));
  Register #(.width(32)) u_t0 (.D(Write_Data), .en(decoder_1_out8), .clk(CLK), .Q(t0), .clr(Reset));
  Register #(.width(32)) u_s0 (.D(Write_Data), .en(decoder_1_out16), .clk(CLK), .Q(s0), .clr(Reset));
  Register #(.width(32)) u_t8 (.D(Write_Data), .en(decoder_1_out24), .clk(CLK), .Q(t8), .clr(Reset));
  Register #(.width(32)) u_at (.D(Write_Data), .en(decoder_1_out1), .clk(CLK), .Q(at), .clr(Reset));
  Register #(.width(32)) u_t1 (.D(Write_Data), .en(decoder_1_out9), .clk(CLK), .Q(t1), .clr(Reset));
  Register #(.width(32)) u_s1 (.D(Write_Data), .en(decoder_1_out17), .clk(CLK), .Q(s1), .clr(Reset));
  Register #(.width(32)) u_t9 (.D(Write_Data), .en(decoder_1_out25), .clk(CLK), .Q(t9), .clr(Reset));
  Register #(.width(32)) u_v0 (.D(Write_Data), .en(decoder_1_out2), .clk(CLK), .Q(v0), .clr(Reset));
  Register #(.width(32)) u_t2 (.D(Write_Data), .en(decoder_1_out10), .clk(CLK), .Q(t2), .clr(Reset));
  Register #(.width(32)) u_s2 (.D(Write_Data), .en(decoder_1_out18), .clk(CLK), .Q(s2), .clr(Reset));
  Register #(.width(32)) u_k0 (.D(Write_Data), .en(decoder_1_out26), .clk(CLK), .Q(k0), .clr(Reset));
  Register #(.width(32)) u_v1 (.D(Write_Data), .en(decoder_1_out3), .clk(CLK), .Q(v1), .clr(Reset));
  Register #(.width(32)) u_t3 (.D(Write_Data), .en(decoder_1_out11), .clk(CLK), .Q(t3), .clr(Reset));
  Register #(.width(32)) u_s3 (.D(Write_Data), .en(decoder_1_out19), .clk(CLK), .Q(s3), .clr(Reset));
  Register #(.width(32)) u_k1 (.D(Write_Data), .en(decoder_1_out27), .clk(CLK), .Q(k1), .clr(Reset));
  Register #(.width(32)) u_a0 (.D(Write_Data), .en(decoder_1_out4), .clk(CLK), .Q(a0), .clr(Reset));
  Register #(.width(32)) u_t4 (.D(Write_Data), .en(decoder_1_out12), .clk(CLK), .Q(t4), .clr(Reset));
  Register #(.width(32)) u_s4 (.D(Write_Data), .en(decoder_1_out20), .clk(CLK), .Q(s4), .clr(Reset));
  Register #(.width(32)) u_gp (.D(Write_Data), .en(decoder_1_out28), .clk(CLK), .Q(gp), .clr(Reset));
  Multiplexer #(.select(5), .width(32)) multiplexer_1 (
    .in0(zero), .in1(at), .in2(v0), .in3(v1), .in4(a0), .in5(a1), .in6(a2), .in7(a3), .in8(t0), .in9(t1),
    .in10(t2), .in11(t3), .in12(t4), .in13(t5), .in14(t6), .in15(t7), .in16(s0), .in17(s1), .in18(s2),
    .in19(s3), .in20(s4), .in21(s5), .in22(s6), .in23(s7), .in24(t8), .in25(t9), .in26(k0), .in27(k1),
    .in28(gp), .in29(sp), .in30(fp), .in31(ra), .out(Read_Data1), .sel(Read_Reg1));
  Multiplexer #(.select(5), .width(32)) multiplexer_2 (
    .in0(zero), .in1(at), .in2(v0), .in3(v1), .in4(a0), .in5(a1), .in6(a2), .in7(a3), .in8(t0), .in9(t1),
    .in10(t2), .in11(t3), .in12(t4), .in13(t5), .in14(t6), .in15(t7), .in16(s0), .in17(s1), .in18(s2),
    .in19(s3), .in20(s4), .in21(s5), .in22(s6), .in23(s7), .in24(t8), .in25(t9), .in26(k0), .in27(k1),
    .in28(gp), .in29(sp), .in30(fp), .in31(ra), .out(Read_Data2), .sel(Read_Reg2));
  Register #(.width(32)) u_a1 (.D(Write_Data), .en(decoder_1_out5), .clk(CLK), .Q(a1), .clr(Reset));
  Register #(.width(32)) u_t5 (.D(Write_Data), .en(decoder_1_out13), .clk(CLK), .Q(t5), .clr(Reset));
  Register #(.width(32)) u_s5 (.D(Write_Data), .en(decoder_1_out21), .clk(CLK), .Q(s5), .clr(Reset));
  Register #(.width(32)) u_sp (.D(Write_Data), .en(decoder_1_out29), .clk(CLK), .Q(sp), .clr(Reset));
  Register #(.width(32)) u_a2 (.D(Write_Data), .en(decoder_1_out6), .clk(CLK), .Q(a2), .clr(Reset));
  Register #(.width(32)) u_t6 (.D(Write_Data), .en(decoder_1_out14), .clk(CLK), .Q(t6), .clr(Reset));
  Register #(.width(32)) u_s6 (.D(Write_Data), .en(decoder_1_out22), .clk(CLK), .Q(s6), .clr(Reset));
  Register #(.width(32)) u_fp (.D(Write_Data), .en(decoder_1_out30), .clk(CLK), .Q(fp), .clr(Reset));
  Register #(.width(32)) u_a3 (.D(Write_Data), .en(decoder_1_out7), .clk(CLK), .Q(a3), .clr(Reset));
  Register #(.width(32)) u_t7 (.D(Write_Data), .en(decoder_1_out15), .clk(CLK), .Q(t7), .clr(Reset));
  Register #(.width(32)) u_s7 (.D(Write_Data), .en(decoder_1_out23), .clk(CLK), .Q(s7), .clr(Reset));
  Register #(.width(32)) u_ra (.D(Write_Data), .en(decoder_1_out31), .clk(CLK), .Q(ra), .clr(Reset));
endmodule

module ALU (
  input  [31:0] In1,
  input  [31:0] In2,
  input  [2:0] ALU_Operation,
  output Zero,
  output [31:0] Result
);

  wire Comp;
  wire [31:0] ADD, And_logic, Nor_logic, Or_logic, SUB;

  Adder #(.width(32)) adder_1 (.a(In1), .b(In2), .out(ADD));  // open: cin, cout
  Subtractor #(.width(32)) subtractor_1 (.a(In1), .b(In2), .out(SUB));  // open: bin, bout
  Comparator #(.width(32)) comparator_1 (.a(In1), .b(In2), .lt(Comp));  // open: gt, eq
  assign And_logic = In1 & In2;  // AND_Gate and_1, 32 bits wide
  assign Nor_logic = ~(In1 | In2);  // NOR_Gate nor_1, 32 bits wide
  assign Or_logic = In1 | In2;  // OR_Gate or_1, 32 bits wide
  Multiplexer #(.select(3), .width(32)) multiplexer_1 (
    .in0(And_logic), .in1(Or_logic), .in2(ADD), .in3(SUB), .in4({{31{1'b0}}, Comp}), .in5(Nor_logic),
    .out(Result), .sel(ALU_Operation));  // open: in6, in7
  Comparator #(.width(32)) comparator_2 (.a(Result), .b({32{1'b0}}), .eq(Zero));  // open: gt, lt

  // Other names for the same wires on the sheet: SLT[0] = Comp
endmodule

module Sign_Ext (
  input  [15:0] In16bit,
  output [31:0] Out32bit
);


  assign Out32bit = {{17{In16bit[15]}}, In16bit[14:0]};
endmodule

module Shift_left2 (
  input  [31:0] In32bit,
  output [31:0] Out32bit
);

  // Probe on In32bit
  // Probe on {In32bit[29:0], 2'b00}

  assign Out32bit = {In32bit[29:0], 2'b00};
endmodule

module Data_memory (
  input  [31:0] Address,
  input  MemWrite,
  input  MemRead,
  input  CLK,
  input  [31:0] MemInput,
  output [31:0] Read_data
);

  RAM #(.addrWidth(24), .dataWidth(32)) ram_1 (
    .addr(Address[25:2]), .we(MemWrite), .oe(MemRead), .clk(CLK), .din(MemInput), .dout(Read_data));
endmodule

module division_4 (
  input  [31:0] i,
  output [23:0] o
);


  assign o = i[25:2];
endmodule

module control (
  input  [5:0] OP,
  output RegDst,
  output ALUSrc,
  output MemtoReg,
  output RegWrite,
  output MemRead,
  output MemWrite,
  output Branch,
  output [1:0] ALUop,
  output Jump,
  output Link
);

  wire and_3_out, and_4_out, not_1_out, not_2_out, not_3_out, not_4_out, not_5_out, not_6_out, not_7_out,
       not_8_out, not_9_out, not_10_out, not_11_out, not_12_out;

  not not_1 (not_1_out, OP[3]);
  not not_2 (not_2_out, OP[1]);
  or or_1 (ALUSrc, OP[1], OP[3]);
  not not_3 (not_3_out, OP[3]);
  not not_4 (not_4_out, OP[2]);
  not not_5 (not_5_out, OP[1]);
  not not_6 (not_6_out, OP[3]);
  not not_7 (not_7_out, OP[3]);
  not not_8 (not_8_out, OP[3]);
  not not_9 (not_9_out, OP[2]);
  not not_10 (not_10_out, OP[1]);
  not not_11 (not_11_out, OP[5]);
  not not_12 (not_12_out, OP[5]);
  and and_1 (RegDst, not_1_out, not_2_out);
  and and_2 (MemtoReg, not_3_out, OP[1]);
  and and_3 (and_3_out, not_4_out, not_5_out);
  and and_4 (and_4_out, not_6_out, OP[0]);
  and and_5 (MemRead, OP[5], not_7_out);
  and and_6 (MemWrite, OP[5], OP[3]);
  and and_7 (ALUop[1], not_8_out, not_9_out, not_10_out);
  and and_8 (Jump, not_11_out, OP[1]);
  and and_9 (Link, not_12_out, OP[0]);
  or or_2 (RegWrite, and_3_out, and_4_out);

  assign ALUop[0] = OP[2];
  assign Branch = OP[2];

  // Other names for the same wires on the sheet: alupo[1:0] = {ALUop[1], OP[2]}
endmodule

module ALUControl (
  input  [1:0] ALUop,
  input  [5:0] Funct,
  output [2:0] Op
);

  wire and_1_out, and_2_out, and_3_out, not_2_out, not_3_out, not_4_out, not_5_out;
  wire [2:0] or_2_out;
  wire [2:2] not_1_out;

  not not_1 (not_1_out[2], ALUop[0]);
  not not_2 (not_2_out, Funct[2]);
  not not_3 (not_3_out, Funct[1]);
  not not_4 (not_4_out, Funct[3]);
  not not_5 (not_5_out, Funct[2]);
  and and_1 (and_1_out, not_2_out, not_3_out);
  and and_2 (and_2_out, Funct[2], Funct[1]);
  and and_3 (and_3_out, not_4_out, not_5_out);
  or or_1 (or_2_out[2], and_1_out, and_2_out, Funct[3]);
  or or_2 (or_2_out[0], and_3_out, Funct[0]);
  Multiplexer #(.width(3)) multiplexer_1 (
    .in0({not_1_out[2], 2'b01}), .in1({or_2_out[2], Funct[2], or_2_out[0]}), .out(Op), .sel(ALUop[1]));

  // Other names for the same wires on the sheet: F = ALUop[1]
endmodule

module instructrion15_0 (
  input  [31:0] i,
  output [5:0] intruc_5_0
);


  assign intruc_5_0 = i[5:0];
endmodule
